# Fritzing sketch Untitled Sketch (saved by Fritzing 1.0.0d)
breadboards: 1

parts:
  Part1 = Arduino Uno (Rev3)
  J1 = Piezo Speaker
  LED1 = smd LED [color="Red (633nm)" package="0805 [SMD]"]

nets:
  N1: Part1.D12/MISO, LED1.cathode
  N2: Part1.D7, J1.pin1
  N3: Part1.5V, J1.pin2, LED1.anode
